// Logisim project DSDProject.circ as structural Verilog: 6 circuits, main circuit sevenSegment
module main (
  input  CarEntranceSensor,
  input  CarExitSensor
);

  wire CarEntrance_green, CarEntrance_red, CarEntrance_yellow, CarExit_green, CarExit_red, CarExit_yellow,
       clock_1_out, DriveThroughCount_a, DriveThroughCount_b, DriveThroughCount_c, DriveThroughCount_d,
       DriveThroughCount_e, DriveThroughCount_f, DriveThroughCount_g, Reset_out, stateactions_1_c_0,
       stateactions_1_c_1, stateactions_1_c_2, stateactions_1_c_3, stateactions_1_le_1, stateactions_1_le_2,
       stateactions_1_lx_1, stateactions_1_lx_2, statecontroller_1_a1, statecontroller_1_a2,
       statecontroller_1_b1, statecontroller_1_b2, statecontroller_1_c1, statecontroller_1_c2,
       statecontroller_1_d1, statecontroller_1_d2, statecontroller_1_e1, statecontroller_1_e2,
       statecontroller_1_f1, statecontroller_1_f2, statecontroller_1_g1, statecontroller_1_g2,
       statecontroller_1_n_0, statecontroller_1_n_1, statecontroller_1_n_2, statecontroller_1_n_3,
       statecontroller_1_n_4, statecontroller_1_n_5;

  Clock clock_1 (.out(clock_1_out));
  Button Reset (.out(Reset_out));
  LED StateCounter ();  // open: in
  _7_Segment_Display u_7_segment_display_1 (
    .g(statecontroller_1_g2), .f(statecontroller_1_f2), .a(statecontroller_1_a2), .b(statecontroller_1_b2),
    .e(statecontroller_1_e2), .d(statecontroller_1_d2), .c(statecontroller_1_c2));  // open: dp
  _7_Segment_Display u_7_segment_display_2 (
    .g(statecontroller_1_g1), .f(statecontroller_1_f1), .a(statecontroller_1_a1), .b(statecontroller_1_b1),
    .e(statecontroller_1_e1), .d(statecontroller_1_d1), .c(statecontroller_1_c1));  // open: dp
  stateController statecontroller_1 (
    .Enter(CarEntranceSensor), .Exit(CarExitSensor), .Clock(clock_1_out), .reset(Reset_out),
    .N_0(statecontroller_1_n_0), .N_1(statecontroller_1_n_1), .N_2(statecontroller_1_n_2),
    .N_3(statecontroller_1_n_3), .N_4(statecontroller_1_n_4), .N_5(statecontroller_1_n_5),
    .g1(statecontroller_1_g1), .f1(statecontroller_1_f1), .a1(statecontroller_1_a1),
    .b1(statecontroller_1_b1), .c1(statecontroller_1_c1), .d1(statecontroller_1_d1),
    .e1(statecontroller_1_e1), .g2(statecontroller_1_g2), .f2(statecontroller_1_f2),
    .a2(statecontroller_1_a2), .b2(statecontroller_1_b2), .c2(statecontroller_1_c2),
    .d2(statecontroller_1_d2), .e2(statecontroller_1_e2));
  stateActions stateactions_1 (
    .S_0(statecontroller_1_n_0), .S_1(statecontroller_1_n_1), .S_2(statecontroller_1_n_2),
    .S_3(statecontroller_1_n_3), .S_4(statecontroller_1_n_4), .S_5(statecontroller_1_n_5),
    .LE_1(stateactions_1_le_1), .LE_2(stateactions_1_le_2), .LX_1(stateactions_1_lx_1),
    .LX_2(stateactions_1_lx_2), .C_0(stateactions_1_c_0), .C_1(stateactions_1_c_1), .C_2(stateactions_1_c_2),
    .C_3(stateactions_1_c_3));
  LED led_1 (.in(CarEntrance_green));
  lightSelector CarEntrance (
    .L_0(stateactions_1_le_1), .L_1(stateactions_1_le_2), .Green(CarEntrance_green),
    .Yellow(CarEntrance_yellow), .Red(CarEntrance_red));
  LED led_2 (.in(CarEntrance_yellow));
  LED led_3 (.in(CarEntrance_red));
  LED led_4 (.in(CarExit_green));
  lightSelector CarExit (
    .L_0(stateactions_1_lx_1), .L_1(stateactions_1_lx_2), .Green(CarExit_green), .Yellow(CarExit_yellow),
    .Red(CarExit_red));
  LED led_5 (.in(CarExit_yellow));
  LED led_6 (.in(CarExit_red));
  sevenSegment DriveThroughCount (
    .d3(stateactions_1_c_0), .d2(stateactions_1_c_1), .d1(stateactions_1_c_2), .d0(stateactions_1_c_3),
    .G(DriveThroughCount_g), .F(DriveThroughCount_f), .A(DriveThroughCount_a), .B(DriveThroughCount_b),
    .C(DriveThroughCount_c), .D(DriveThroughCount_d), .E(DriveThroughCount_e));
  _7_Segment_Display u_7_segment_display_3 (
    .g(DriveThroughCount_g), .f(DriveThroughCount_f), .a(DriveThroughCount_a), .b(DriveThroughCount_b),
    .e(DriveThroughCount_e), .d(DriveThroughCount_d), .c(DriveThroughCount_c));  // open: dp
endmodule

module stateController (
  input  Enter,
  input  Exit,
  input  Clock,
  input  reset,
  output N_0,
  output N_1,
  output N_2,
  output N_3,
  output N_4,
  output N_5,
  output g1,
  output f1,
  output a1,
  output b1,
  output c1,
  output d1,
  output e1,
  output g2,
  output f2,
  output a2,
  output b2,
  output c2,
  output d2,
  output e2
);

  wire and_1_out, and_2_out, and_3_out, and_4_out, and_5_out, and_6_out, and_7_out, and_8_out, and_9_out,
       and_10_out, and_11_out, and_12_out, and_13_out, and_14_out, and_15_out, and_16_out, and_17_out,
       and_18_out, and_19_out, and_20_out, and_21_out, and_22_out, and_23_out, and_24_out, and_25_out,
       and_26_out, and_27_out, and_28_out, and_29_out, and_30_out, and_31_out, and_32_out, and_33_out,
       and_34_out, and_35_out, and_36_out, and_37_out, and_38_out, and_39_out, and_40_out, and_41_out,
       and_42_out, and_43_out, and_44_out, and_45_out, and_46_out, and_47_out, and_48_out, and_49_out,
       and_50_out, and_51_out, and_52_out, and_53_out, and_54_out, and_55_out, and_56_out, and_57_out,
       and_58_out, and_59_out, and_60_out, and_61_out, and_62_out, and_63_out, and_64_out, and_65_out,
       and_66_out, and_67_out, and_68_out, and_69_out, and_70_out, and_71_out, and_72_out, and_73_out,
       and_74_out, and_75_out, and_76_out, not_1_out, not_2_out, not_3_out, not_4_out, not_5_out, not_6_out,
       not_7_out, not_8_out;
  wire [5:0] or_1_out;

  not not_1 (not_1_out, N_0);
  not not_2 (not_2_out, N_1);
  not not_3 (not_3_out, N_2);
  not not_4 (not_4_out, N_3);
  not not_5 (not_5_out, N_4);
  not not_6 (not_6_out, N_5);
  not not_7 (not_7_out, Enter);
  not not_8 (not_8_out, Exit);
  and and_1 (and_1_out, not_2_out, not_3_out, N_3, N_4, N_5, Exit);
  and and_2 (and_2_out, not_2_out, N_2, not_4_out, not_5_out, Exit);
  and and_3 (and_3_out, not_2_out, N_2, not_4_out, not_5_out, N_5);
  and and_4 (and_4_out, N_1, N_2, N_3, N_4, N_5);
  and and_5 (and_5_out, N_0, not_5_out, not_8_out);
  and and_6 (and_6_out, N_0, N_5);
  and and_7 (and_7_out, N_0, N_3, not_5_out);
  and and_8 (and_8_out, not_1_out, not_3_out, not_4_out, N_4, N_5, Exit);
  and and_9 (and_9_out, not_1_out, not_2_out, not_3_out, N_3, not_6_out, Exit);
  and and_10 (and_10_out, not_1_out, not_3_out, N_3, not_5_out, Exit);
  and and_11 (and_11_out, not_2_out, N_2, N_3, N_4, N_5);
  and and_12 (and_12_out, N_1, not_5_out, not_8_out);
  and and_13 (and_13_out, N_1, not_3_out, N_5);
  and and_14 (and_14_out, N_1, not_4_out, N_5);
  and and_15 (and_15_out, N_1, N_2, not_5_out);
  and and_16 (and_16_out, N_0, not_3_out, not_4_out, not_5_out, not_6_out, Exit);
  and and_17 (and_17_out, not_1_out, not_2_out, not_5_out, N_5, Exit);
  and and_18 (and_18_out, not_1_out, not_2_out, not_3_out, N_4, not_6_out, Exit);
  and and_19 (and_19_out, not_3_out, N_3, N_4, N_5, Enter, not_8_out);
  and and_20 (and_20_out, N_2, not_5_out, not_8_out);
  and and_21 (and_21_out, N_2, not_4_out, N_5);
  and and_22 (and_22_out, N_2, N_3, not_5_out);
  and and_23 (and_23_out, N_1, not_3_out, not_4_out, not_5_out, not_6_out, Exit);
  and and_24 (and_24_out, N_1, not_3_out, N_3, N_4, N_5);
  and and_25 (and_25_out, N_0, not_3_out, not_4_out, not_5_out, not_6_out, Exit);
  and and_26 (and_26_out, N_0, N_3, N_4, Enter);
  and and_27 (and_27_out, N_0, N_3, N_4, N_5);
  and and_28 (and_28_out, N_0, N_2, N_5);
  and and_29 (and_29_out, N_0, N_2, N_4);
  and and_30 (and_30_out, not_1_out, not_2_out, not_3_out, N_4, not_6_out, Exit);
  and and_31 (and_31_out, not_4_out, N_4, N_5, Enter, not_8_out);
  and and_32 (and_32_out, not_1_out, not_2_out, not_3_out, N_3, not_6_out);
  and and_33 (and_33_out, not_1_out, not_2_out, not_3_out, N_3, not_7_out, not_8_out);
  and and_34 (and_34_out, N_3, not_5_out, not_8_out);
  and and_35 (and_35_out, not_1_out, not_3_out, N_3, N_4, not_6_out, Enter);
  and and_36 (and_36_out, N_2, not_4_out, not_5_out, not_6_out, Exit);
  and and_37 (and_37_out, N_2, not_4_out, N_4, N_5);
  and and_38 (and_38_out, N_2, N_3, not_5_out, N_5);
  and and_39 (and_39_out, N_1, not_4_out, not_5_out, not_6_out, Exit);
  and and_40 (and_40_out, N_1, not_4_out, N_4, N_5);
  and and_41 (and_41_out, N_1, N_3, not_5_out, N_5);
  and and_42 (and_42_out, N_1, N_2, N_4, not_6_out);
  and and_43 (and_43_out, N_0, not_3_out, not_4_out, not_6_out, Exit);
  and and_44 (and_44_out, N_0, not_3_out, not_4_out, N_4);
  and and_45 (and_45_out, N_0, not_3_out, N_4, not_6_out, not_7_out);
  and and_46 (and_46_out, N_0, N_3, not_6_out, not_7_out, not_8_out);
  and and_47 (and_47_out, N_0, N_3, not_5_out, N_5);
  and and_48 (and_48_out, not_5_out, N_5, Exit);
  and and_49 (and_49_out, not_5_out, N_5, Enter);
  and and_50 (and_50_out, not_1_out, not_2_out, not_3_out, N_4, not_6_out);
  and and_51 (and_51_out, not_1_out, not_2_out, not_3_out, N_4, not_7_out);
  and and_52 (and_52_out, not_2_out, not_3_out, not_4_out, N_4, not_6_out);
  and and_53 (and_53_out, not_3_out, N_4, not_6_out, not_7_out);
  and and_54 (and_54_out, not_1_out, not_2_out, not_3_out, N_4, Exit);
  and and_55 (and_55_out, not_1_out, not_2_out, not_3_out, N_3, Exit);
  and and_56 (and_56_out, not_1_out, not_2_out, N_2, not_5_out, Exit);
  and and_57 (and_57_out, N_2, not_5_out, N_5);
  and and_58 (and_58_out, N_2, N_3, N_4, not_6_out, Enter);
  and and_59 (and_59_out, N_1, not_5_out, N_5);
  and and_60 (and_60_out, N_0, not_5_out, N_5);
  and and_61 (and_61_out, not_1_out, not_2_out, not_3_out, not_6_out, Enter);
  and and_62 (and_62_out, not_1_out, not_5_out, not_6_out, Enter, not_8_out);
  and and_63 (and_63_out, not_3_out, not_5_out, not_6_out, Enter, not_8_out);
  and and_64 (and_64_out, not_4_out, not_5_out, not_6_out, Enter, not_8_out);
  and and_65 (and_65_out, not_1_out, not_2_out, not_3_out, N_5, not_7_out);
  and and_66 (and_66_out, not_1_out, not_2_out, not_3_out, N_4, Exit);
  and and_67 (and_67_out, not_1_out, not_3_out, N_4, not_6_out, not_7_out, Exit);
  and and_68 (and_68_out, not_3_out, not_4_out, N_4, not_6_out, Enter);
  and and_69 (and_69_out, not_1_out, not_2_out, not_3_out, N_3, Exit);
  and and_70 (and_70_out, not_1_out, not_2_out, N_2, not_4_out, not_5_out, Exit);
  and and_71 (and_71_out, not_1_out, not_2_out, N_2, not_4_out, not_5_out, N_5);
  and and_72 (and_72_out, N_2, N_3, N_4, not_6_out, not_7_out);
  and and_73 (and_73_out, N_1, not_3_out, N_4, not_6_out, not_7_out);
  and and_74 (and_74_out, N_1, not_4_out, N_4, not_6_out, Enter);
  and and_75 (and_75_out, N_0, N_3, N_4, not_6_out, not_7_out);
  and and_76 (and_76_out, N_0, N_2, N_4, not_6_out, Enter);
  or or_1 (or_1_out[0], and_1_out, and_2_out, and_3_out, and_4_out, and_5_out, and_6_out, and_7_out);
  or or_2 (or_1_out[1], and_8_out, and_9_out, and_10_out, and_11_out, and_12_out, and_13_out, and_14_out, and_15_out, and_16_out);
  or or_3 (or_1_out[2], and_17_out, and_18_out, and_19_out, and_20_out, and_21_out, and_22_out, and_23_out, and_24_out, and_25_out, and_26_out, and_27_out, and_28_out, and_29_out);
  or or_4 (or_1_out[3], and_30_out, and_31_out, and_32_out, and_33_out, and_34_out, and_35_out, and_36_out, and_37_out, and_38_out, and_39_out, and_40_out, and_41_out, and_42_out, and_43_out, and_44_out, and_45_out, and_46_out, and_47_out);
  or or_5 (or_1_out[4], and_48_out, and_49_out, and_50_out, and_51_out, and_52_out, and_53_out, and_54_out, and_55_out, and_56_out, and_57_out, and_58_out, and_59_out, and_60_out);
  or or_6 (or_1_out[5], and_61_out, and_62_out, and_63_out, and_64_out, and_65_out, and_66_out, and_67_out, and_68_out, and_69_out, and_70_out, and_71_out, and_72_out, and_73_out, and_74_out, and_75_out, and_76_out);
  Register #(.width(6)) register_1 (
    .D(or_1_out), .clk(Clock), .Q({N_5, N_4, N_3, N_2, N_1, N_0}), .clr(reset));  // open: en
  stateCounter statecounter_1 (
    .S_0(N_0), .S_1(N_1), .S_2(N_2), .S_3(N_3), .S_4(N_4), .S_5(N_5), .g1(g1), .f1(f1), .a1(a1), .b1(b1),
    .c1(c1), .d1(d1), .e1(e1), .g2(g2), .f2(f2), .a2(a2), .b2(b2), .c2(c2), .d2(d2), .e2(e2));
endmodule

module sevenSegment (
  input  d3,
  input  d2,
  input  d1,
  input  d0,
  output G,
  output F,
  output A,
  output B,
  output C,
  output D,
  output E
);

  wire and_1_out, and_2_out, and_3_out, and_4_out, and_5_out, and_6_out, and_7_out, and_8_out, and_9_out,
       and_10_out, and_11_out, and_12_out, and_13_out, and_14_out, and_15_out, and_16_out, and_17_out,
       and_18_out, and_19_out, and_20_out, and_21_out, and_22_out, and_23_out, and_24_out, and_25_out,
       and_26_out, and_27_out, and_28_out, and_29_out, and_30_out, and_31_out, and_32_out, and_33_out,
       and_34_out, and_35_out, and_36_out, and_37_out, and_38_out, and_39_out, and_40_out, and_41_out,
       and_42_out, and_43_out, and_44_out, and_45_out, and_46_out, and_47_out, not_1_out, not_2_out,
       not_3_out, not_4_out, or_1_out, or_2_out, or_3_out, or_4_out, or_5_out, or_7_out, or_9_out, or_10_out,
       or_11_out, or_12_out, or_15_out, or_17_out;

  not not_1 (not_1_out, d1);
  not not_2 (not_2_out, d0);
  not not_3 (not_3_out, d3);
  not not_4 (not_4_out, d2);
  and and_1 (and_1_out, not_3_out, not_4_out);
  and and_2 (and_2_out, not_3_out, d2);
  and and_3 (and_3_out, d3, not_4_out);
  and and_4 (and_4_out, not_3_out, not_1_out);
  and and_5 (and_5_out, not_3_out, d1);
  and and_6 (and_6_out, not_4_out, not_1_out);
  and and_7 (and_7_out, not_3_out, d0);
  and and_8 (and_8_out, not_3_out, not_4_out);
  and and_9 (and_9_out, not_3_out, not_4_out);
  and and_10 (and_10_out, not_4_out, not_1_out);
  and and_11 (and_11_out, not_3_out, d1);
  and and_12 (and_12_out, not_3_out, not_1_out);
  and and_13 (and_13_out, not_3_out, d2);
  and and_14 (and_14_out, not_3_out, d2);
  and and_15 (and_15_out, d3, not_4_out);
  and and_16 (and_16_out, not_3_out, not_4_out);
  and and_17 (and_17_out, not_3_out, d2);
  and and_18 (and_18_out, not_3_out, d2);
  and and_19 (and_19_out, d3, not_4_out);
  and and_20 (and_20_out, and_1_out, not_2_out);
  and and_21 (and_21_out, not_3_out, d1);
  and and_22 (and_22_out, and_2_out, d0);
  and and_23 (and_23_out, and_3_out, not_1_out);
  and and_24 (and_24_out, not_3_out, not_4_out);
  and and_25 (and_25_out, and_4_out, not_2_out);
  and and_26 (and_26_out, not_4_out, not_1_out);
  and and_27 (and_27_out, and_5_out, d0);
  or or_1 (or_1_out, and_6_out, and_7_out);
  and and_28 (and_28_out, not_3_out, d2);
  and and_29 (and_29_out, and_8_out, not_2_out);
  and and_30 (and_30_out, and_9_out, d1);
  and and_31 (and_31_out, not_3_out, d1);
  and and_32 (and_32_out, not_3_out, d2);
  and and_33 (and_33_out, not_1_out, d0);
  and and_34 (and_34_out, d3, not_4_out);
  and and_35 (and_35_out, and_10_out, not_2_out);
  and and_36 (and_36_out, and_11_out, not_2_out);
  and and_37 (and_37_out, and_12_out, not_2_out);
  and and_38 (and_38_out, and_13_out, not_1_out);
  and and_39 (and_39_out, and_14_out, not_2_out);
  and and_40 (and_40_out, and_15_out, not_1_out);
  and and_41 (and_41_out, and_16_out, d1);
  and and_42 (and_42_out, and_17_out, not_1_out);
  and and_43 (and_43_out, and_18_out, not_2_out);
  and and_44 (and_44_out, and_19_out, not_1_out);
  or or_2 (or_2_out, and_20_out, and_21_out);
  or or_3 (or_3_out, and_22_out, and_23_out);
  or or_4 (or_4_out, and_24_out, and_25_out);
  or or_5 (or_5_out, and_26_out, and_27_out);
  or or_6 (C, or_1_out, and_28_out);
  or or_7 (or_7_out, and_29_out, and_30_out);
  and and_45 (and_45_out, and_31_out, not_2_out);
  and and_46 (and_46_out, and_32_out, and_33_out);
  and and_47 (and_47_out, and_34_out, not_1_out);
  or or_8 (E, and_35_out, and_36_out);
  or or_9 (or_9_out, and_37_out, and_38_out);
  or or_10 (or_10_out, and_39_out, and_40_out);
  or or_11 (or_11_out, and_41_out, and_42_out);
  or or_12 (or_12_out, and_43_out, and_44_out);
  or or_13 (A, or_2_out, or_3_out);
  or or_14 (B, or_4_out, or_5_out);
  or or_15 (or_15_out, or_7_out, and_45_out);
  or or_16 (D, or_15_out, or_17_out);
  or or_17 (or_17_out, and_46_out, and_47_out);
  or or_18 (F, or_9_out, or_10_out);
  or or_19 (G, or_11_out, or_12_out);
endmodule

module stateActions (
  input  S_0,
  input  S_1,
  input  S_2,
  input  S_3,
  input  S_4,
  input  S_5,
  output LE_1,
  output LE_2,
  output LX_1,
  output LX_2,
  output C_0,
  output C_1,
  output C_2,
  output C_3
);

  wire and_1_out, and_2_out, and_3_out, and_4_out, and_5_out, and_6_out, and_7_out, and_8_out, and_9_out,
       and_10_out, and_11_out, and_12_out, and_13_out, and_14_out, and_15_out, and_16_out, and_17_out,
       and_18_out, and_19_out, and_20_out, and_21_out, and_22_out, and_23_out, and_24_out, and_25_out,
       and_26_out, and_27_out, and_28_out, and_29_out, and_30_out, and_31_out, and_32_out, and_33_out,
       and_34_out, and_35_out, and_36_out, and_37_out, and_38_out, and_39_out, and_40_out, and_41_out,
       and_42_out, and_43_out, not_1_out, not_2_out, not_3_out, not_4_out, not_5_out, not_6_out;

  not not_1 (not_1_out, S_0);
  not not_2 (not_2_out, S_1);
  not not_3 (not_3_out, S_2);
  not not_4 (not_4_out, S_3);
  not not_5 (not_5_out, S_4);
  not not_6 (not_6_out, S_5);
  and and_1 (and_1_out, not_1_out, not_2_out, S_2, not_4_out, S_4, not_6_out);
  and and_2 (and_2_out, S_2, S_3, not_5_out);
  and and_3 (and_3_out, S_1, not_5_out);
  and and_4 (and_4_out, S_0, not_5_out);
  and and_5 (and_5_out, S_2, S_4, S_5);
  and and_6 (and_6_out, S_1, S_4, S_5);
  or or_1 (LE_2, and_5_out, and_6_out, and_7_out);
  and and_7 (and_7_out, S_0, S_4, S_5);
  and and_8 (and_8_out, not_1_out, not_2_out, not_3_out);
  and and_9 (and_9_out, not_1_out, not_2_out, not_4_out, not_5_out);
  and and_10 (and_10_out, not_1_out, not_2_out, not_4_out, S_5);
  and and_11 (and_11_out, S_4, S_5);
  and and_12 (and_12_out, S_3, S_4);
  and and_13 (and_13_out, S_1, S_4);
  and and_14 (and_14_out, S_0, S_4);
  and and_15 (and_15_out, not_1_out, not_2_out, S_2, not_4_out, S_4, not_6_out);
  and and_16 (and_16_out, S_2, S_3, not_5_out, S_5);
  and and_17 (and_17_out, S_1, not_5_out, S_5);
  and and_18 (and_18_out, S_0, not_5_out, S_5);
  and and_19 (and_19_out, not_2_out, S_2, not_4_out, not_5_out);
  and and_20 (and_20_out, S_0, S_3, S_4, S_5);
  or or_2 (C_0, and_19_out, and_20_out, and_21_out);
  and and_21 (and_21_out, S_0, S_2);
  and and_22 (and_22_out, not_1_out, not_2_out, not_3_out, S_3);
  and and_23 (and_23_out, not_1_out, not_3_out, S_3, S_4, S_5);
  and and_24 (and_24_out, S_1, S_2);
  and and_25 (and_25_out, S_0, not_3_out, not_4_out);
  and and_26 (and_26_out, S_0, not_3_out, not_6_out);
  and and_27 (and_27_out, S_0, S_3, not_5_out, S_5);
  and and_28 (and_28_out, not_1_out, not_2_out, not_3_out, S_4);
  and and_29 (and_29_out, not_3_out, S_4, not_6_out);
  and and_30 (and_30_out, S_2, S_3, S_4, S_5);
  and and_31 (and_31_out, S_1, not_3_out, not_4_out);
  and and_32 (and_32_out, S_1, not_3_out, not_5_out);
  and and_33 (and_33_out, S_1, not_3_out, not_6_out);
  and and_34 (and_34_out, S_0, not_3_out, not_4_out);
  and and_35 (and_35_out, S_0, not_3_out, not_5_out);
  and and_36 (and_36_out, S_0, not_3_out, not_6_out);
  and and_37 (and_37_out, not_1_out, not_2_out, not_3_out, S_5);
  and and_38 (and_38_out, not_1_out, not_2_out, not_5_out, S_5);
  and and_39 (and_39_out, not_4_out, S_4, S_5);
  and and_40 (and_40_out, S_3, not_5_out, S_5);
  and and_41 (and_41_out, S_2, S_3, not_6_out);
  and and_42 (and_42_out, S_1, S_3, not_6_out);
  and and_43 (and_43_out, S_0, S_3, not_6_out);
  or or_3 (LE_1, and_1_out, and_2_out, and_3_out, and_4_out);
  or or_4 (LX_1, and_8_out, and_9_out, and_10_out, and_11_out, and_12_out, and_13_out, and_14_out);
  or or_5 (LX_2, and_15_out, and_16_out, and_17_out, and_18_out);
  or or_6 (C_1, and_22_out, and_23_out, and_24_out, and_25_out, and_26_out, and_27_out);
  or or_7 (C_2, and_28_out, and_29_out, and_30_out, and_31_out, and_32_out, and_33_out, and_34_out, and_35_out, and_36_out);
  or or_8 (C_3, and_37_out, and_38_out, and_39_out, and_40_out, and_41_out, and_42_out, and_43_out);
endmodule

module lightSelector (
  input  L_0,
  input  L_1,
  output Green,
  output Yellow,
  output Red
);

  wire not_1_out, not_2_out;

  not not_1 (not_1_out, L_0);
  not not_2 (not_2_out, L_1);
  and and_1 (Green, not_1_out, not_2_out);
  and and_2 (Red, L_0, not_2_out);

  assign Yellow = L_1;
endmodule

module stateCounter (
  input  S_0,
  input  S_1,
  input  S_2,
  input  S_3,
  input  S_4,
  input  S_5,
  output g1,
  output f1,
  output a1,
  output b1,
  output c1,
  output d1,
  output e1,
  output g2,
  output f2,
  output a2,
  output b2,
  output c2,
  output d2,
  output e2
);

  wire and_1_out, and_2_out, and_3_out, and_4_out, and_5_out, and_6_out, and_7_out, and_8_out, and_9_out,
       and_10_out, and_11_out, and_12_out, and_13_out, and_14_out, and_15_out, and_16_out, and_17_out,
       and_18_out, and_19_out, and_20_out, and_21_out, and_22_out, and_23_out, and_24_out, and_25_out,
       and_26_out, and_27_out, and_28_out, and_29_out, and_30_out, and_31_out, and_32_out, and_33_out,
       and_34_out, and_35_out, and_36_out, and_37_out, and_38_out, and_39_out, and_40_out, and_41_out,
       and_42_out, and_43_out, and_44_out, and_45_out, and_46_out, and_47_out, and_48_out, and_49_out,
       and_50_out, and_51_out, and_52_out, and_53_out, and_54_out, and_55_out, and_56_out, and_57_out,
       and_58_out, and_59_out, and_60_out, and_61_out, and_62_out, and_63_out, and_64_out, and_65_out,
       and_66_out, and_67_out, and_68_out, and_69_out, and_70_out, and_71_out, and_72_out, and_73_out,
       and_74_out, and_75_out, and_76_out, and_77_out, and_78_out, and_79_out, and_80_out, and_81_out,
       and_82_out, and_83_out, and_84_out, and_85_out, and_86_out, and_87_out, and_88_out, and_89_out,
       and_90_out, and_91_out, and_92_out, and_93_out, and_94_out, and_95_out, and_96_out, and_97_out,
       and_98_out, and_99_out, and_100_out, and_101_out, and_102_out, and_103_out, and_104_out, and_105_out,
       and_106_out, not_1_out, not_2_out, not_3_out, not_4_out, not_5_out, not_6_out;

  not not_1 (not_1_out, S_0);
  not not_2 (not_2_out, S_1);
  not not_3 (not_3_out, S_2);
  not not_4 (not_4_out, S_3);
  not not_5 (not_5_out, S_4);
  not not_6 (not_6_out, S_5);
  and and_1 (and_1_out, not_3_out, not_4_out, S_4);
  and and_2 (and_2_out, not_1_out, not_2_out, S_3, not_5_out);
  and and_3 (and_3_out, not_2_out, S_3, not_6_out);
  and and_4 (and_4_out, not_1_out, S_2, not_5_out);
  and and_5 (and_5_out, not_2_out, S_2, S_3);
  and and_6 (and_6_out, S_1, not_4_out, not_6_out);
  and and_7 (and_7_out, S_1, not_3_out, S_4);
  and and_8 (and_8_out, S_0, not_3_out, not_4_out);
  and and_9 (and_9_out, S_0, S_4);
  and and_10 (and_10_out, S_0, S_3, not_6_out);
  and and_11 (and_11_out, not_1_out, not_3_out, not_5_out, not_6_out);
  and and_12 (and_12_out, not_1_out, not_2_out, not_3_out, S_3, not_5_out);
  and and_13 (and_13_out, not_2_out, not_3_out, S_3, not_6_out);
  and and_14 (and_14_out, not_1_out, S_2, not_4_out, not_5_out);
  and and_15 (and_15_out, not_1_out, S_2, not_4_out, not_6_out);
  and and_16 (and_16_out, S_2, not_4_out, not_5_out, not_6_out);
  and and_17 (and_17_out, not_2_out, S_2, S_3, S_4);
  and and_18 (and_18_out, S_1, not_5_out, not_6_out);
  and and_19 (and_19_out, S_1, not_3_out, not_4_out, S_4);
  and and_20 (and_20_out, S_1, S_2, not_5_out);
  and and_21 (and_21_out, S_1, S_2, not_6_out);
  and and_22 (and_22_out, S_0, not_3_out, S_4);
  and and_23 (and_23_out, S_0, S_3, not_6_out);
  and and_24 (and_24_out, not_1_out, not_3_out, not_4_out, not_6_out);
  and and_25 (and_25_out, not_2_out, not_4_out, not_5_out, not_6_out);
  and and_26 (and_26_out, not_1_out, not_3_out, S_4);
  and and_27 (and_27_out, not_1_out, not_4_out, S_4, not_6_out);
  and and_28 (and_28_out, not_2_out, S_3, S_5);
  and and_29 (and_29_out, not_1_out, not_2_out, S_2, not_5_out);
  and and_30 (and_30_out, not_2_out, S_2, not_4_out, not_6_out);
  and and_31 (and_31_out, S_1, not_4_out, S_5);
  and and_32 (and_32_out, S_1, S_3, not_6_out);
  and and_33 (and_33_out, S_1, S_2, not_5_out, S_5);
  and and_34 (and_34_out, S_0, not_3_out, not_5_out);
  and and_35 (and_35_out, S_0, S_4, S_5);
  and and_36 (and_36_out, S_0, S_3, S_4);
  and and_37 (and_37_out, not_2_out, not_4_out, not_5_out);
  and and_38 (and_38_out, not_2_out, not_4_out, not_6_out);
  and and_39 (and_39_out, not_1_out, not_3_out, S_4, S_5);
  and and_40 (and_40_out, not_1_out, not_4_out, S_4, S_5);
  and and_41 (and_41_out, not_1_out, S_3, not_5_out, not_6_out);
  and and_42 (and_42_out, not_2_out, S_2, not_5_out);
  and and_43 (and_43_out, S_2, not_5_out, not_6_out);
  and and_44 (and_44_out, S_2, S_3, not_6_out);
  and and_45 (and_45_out, S_1, not_3_out, S_5);
  and and_46 (and_46_out, S_1, not_3_out, S_4);
  and and_47 (and_47_out, S_1, S_3);
  and and_48 (and_48_out, S_0, S_4, not_6_out);
  and and_49 (and_49_out, S_0, S_3, S_5);
  and and_50 (and_50_out, S_0, S_2);
  and and_51 (and_51_out, not_1_out, not_3_out, not_5_out);
  and and_52 (and_52_out, not_2_out, not_3_out, S_3);
  and and_53 (and_53_out, not_3_out, S_3, not_5_out);
  and and_54 (and_54_out, not_1_out, S_2, not_4_out);
  and and_55 (and_55_out, S_2, S_3, S_4);
  and and_56 (and_56_out, S_1, not_4_out);
  and and_57 (and_57_out, S_1, not_5_out);
  and and_58 (and_58_out, S_0, not_3_out, S_4);
  and and_59 (and_59_out, S_0, S_2, not_5_out);
  and and_60 (and_60_out, not_1_out, not_2_out, not_4_out, not_6_out);
  and and_61 (and_61_out, not_1_out, not_3_out, not_4_out, S_4);
  and and_62 (and_62_out, not_1_out, not_3_out, S_4, not_6_out);
  and and_63 (and_63_out, not_1_out, not_4_out, S_4, not_6_out);
  and and_64 (and_64_out, not_1_out, not_2_out, S_3, not_5_out, S_5);
  and and_65 (and_65_out, not_1_out, not_2_out, S_2, not_5_out);
  and and_66 (and_66_out, not_2_out, S_2, not_4_out, not_6_out);
  and and_67 (and_67_out, not_1_out, S_2, not_5_out, S_5);
  and and_68 (and_68_out, not_2_out, S_2, S_3, S_5);
  and and_69 (and_69_out, S_2, S_3, not_5_out, S_5);
  and and_70 (and_70_out, S_1, not_3_out, not_6_out);
  and and_71 (and_71_out, S_1, not_3_out, S_4);
  and and_72 (and_72_out, S_1, S_3, not_6_out);
  and and_73 (and_73_out, S_0, not_3_out, not_4_out, not_5_out);
  and and_74 (and_74_out, S_0, not_3_out, not_5_out, not_6_out);
  and and_75 (and_75_out, S_0, not_4_out, not_5_out, not_6_out);
  and and_76 (and_76_out, S_0, S_4, S_5);
  and and_77 (and_77_out, S_0, S_3, S_4);
  and and_78 (and_78_out, not_2_out, not_4_out, not_5_out, not_6_out);
  and and_79 (and_79_out, not_1_out, not_3_out, S_4, not_6_out);
  and and_80 (and_80_out, not_2_out, S_2, not_4_out, not_6_out);
  and and_81 (and_81_out, not_1_out, S_2, S_3, not_5_out, not_6_out);
  and and_82 (and_82_out, S_1, not_3_out, not_6_out);
  and and_83 (and_83_out, S_1, S_4, not_6_out);
  and and_84 (and_84_out, S_0, not_3_out, not_5_out, not_6_out);
  and and_85 (and_85_out, S_0, S_3, S_4, not_6_out);
  and and_86 (and_86_out, S_1, S_3);
  and and_87 (and_87_out, S_1, S_2);
  or or_1 (g2, and_86_out, and_87_out, S_0);
  and and_88 (and_88_out, not_1_out, not_2_out, not_3_out);
  and and_89 (and_89_out, not_1_out, not_2_out, not_4_out, not_5_out);
  or or_2 (f2, and_88_out, and_89_out, and_90_out);
  and and_90 (and_90_out, S_0, S_2);
  and and_91 (and_91_out, not_1_out, not_2_out, not_4_out, not_5_out);
  and and_92 (and_92_out, not_2_out, not_3_out);
  and and_93 (and_93_out, not_3_out, S_3);
  and and_94 (and_94_out, S_1, S_2);
  and and_95 (and_95_out, not_3_out, not_4_out);
  or or_3 (c2, not_2_out, and_95_out, and_96_out);
  and and_96 (and_96_out, S_2, S_3, S_4);
  and and_97 (and_97_out, not_1_out, not_2_out, not_4_out, not_5_out);
  and and_98 (and_98_out, not_2_out, not_3_out);
  and and_99 (and_99_out, not_3_out, S_3);
  and and_100 (and_100_out, S_1, S_2);
  and and_101 (and_101_out, not_1_out, not_2_out, not_3_out);
  and and_102 (and_102_out, not_1_out, not_2_out, not_4_out, not_5_out);
  and and_103 (and_103_out, not_1_out, not_3_out, S_3);
  and and_104 (and_104_out, S_1, S_3, not_5_out);
  and and_105 (and_105_out, S_1, S_2, not_4_out);
  and and_106 (and_106_out, S_1, S_2, not_5_out);
  or or_4 (g1, and_1_out, and_2_out, and_3_out, and_4_out, and_5_out, and_6_out, and_7_out, and_8_out, and_9_out, and_10_out);
  or or_5 (f1, and_11_out, and_12_out, and_13_out, and_14_out, and_15_out, and_16_out, and_17_out, and_18_out, and_19_out, and_20_out, and_21_out, and_22_out, and_23_out);
  or or_6 (a1, and_24_out, and_25_out, and_26_out, and_27_out, and_28_out, and_29_out, and_30_out, and_31_out, and_32_out, and_33_out, and_34_out, and_35_out, and_36_out);
  or or_7 (b1, and_37_out, and_38_out, and_39_out, and_40_out, and_41_out, and_42_out, and_43_out, and_44_out, and_45_out, and_46_out, and_47_out, and_48_out, and_49_out, and_50_out);
  or or_8 (c1, and_51_out, S_5, and_52_out, and_53_out, and_54_out, and_55_out, and_56_out, and_57_out, and_58_out, and_59_out);
  or or_9 (d1, and_60_out, and_61_out, and_62_out, and_63_out, and_64_out, and_65_out, and_66_out, and_67_out, and_68_out, and_69_out, and_70_out, and_71_out, and_72_out, and_73_out, and_74_out, and_75_out, and_76_out, and_77_out);
  or or_10 (e1, and_78_out, and_79_out, and_80_out, and_81_out, and_82_out, and_83_out, and_84_out, and_85_out);
  or or_11 (a2, and_91_out, and_92_out, and_93_out, and_94_out);
  or or_12 (d2, and_97_out, and_98_out, and_99_out, and_100_out);
  or or_13 (e2, and_101_out, and_102_out, and_103_out, and_104_out, and_105_out, and_106_out);

  assign b2 = 1'b1;
endmodule
